# Fritzing sketch ESP32_CAM_MOSFET (saved by Fritzing 1.0.0)
breadboards: 1

parts:
  ESP32-WROVER-DEV = ESP32-WROVER-DEV con cámara OV2640
  Fuente_12V = Fuente 12 V CD
  Q1_IRFZ44N = IRFZ44N MOSFET canal N [package="TO220 [THT]"]
  U1_74LS07 = 74LS07 buffer colector abierto [package="DIP14 [THT]"]
  R1_1k = Resistor [resistance=1kΩ package=THT]
  R2_4_7k = Resistor [resistance=4.7kΩ package=THT]
  R3_100 = Resistor [resistance=100Ω package=THT]
  Modulo_LED_12V = Módulo LED 12 V

nets:
  N1: ESP32-WROVER-DEV.33, U1_74LS07.1A, R1_1k.Pin_0
  GND: ESP32-WROVER-DEV.GND, Fuente_12V.GND, Q1_IRFZ44N.source, U1_74LS07.GND, R1_1k.Pin_1
  VCC: ESP32-WROVER-DEV.VCC, U1_74LS07.VCC
  +12V: Fuente_12V.+12V, R2_4_7k.Pin_1, Modulo_LED_12V.+12V
  N2: Q1_IRFZ44N.gate, R3_100.Pin_1
  N3: Q1_IRFZ44N.drain, Modulo_LED_12V.GND
  N4: U1_74LS07.1Y, R2_4_7k.Pin_0, R3_100.Pin_0

custom parts:
  ESP32-WROVER-DEV con cámara OV2640: ESP32-WROVER-DEV con cámara OV2640 de Tostatronic (tostatronic.com). Pieza creada por Tostatronic (Ing. Jorge Alvarado).
  Fuente 12 V CD: Fuente/eliminador de 12 V CD con cables rojo (+) y negro (−).
  IRFZ44N MOSFET canal N: MOSFET canal N, 55 V, 49 A, 17.5 mΩ con VGS = 10 V.
  74LS07 buffer colector abierto: Seis buffers no inversores con salida de colector abierto (hasta 30 V).
  Módulo LED 12 V: Módulo de LEDs de 12 V con cable rojo (+) y negro (−).
